# Fritzing sketch Guitar Hack Diagram (saved by Fritzing 1.0.0rc)
circuit board: 8.46667cm x 5.64444cm
breadboards: 1

parts:
  Part1 = Arduino Pro Micro (Clone)
  OLED1 = OLED 128x64 I2C Monochrome Display GND-VDD
  TRS1 = Audio Jack (TRS) 3.5mm [package="4Ucon 08780 [THT]"]
  R3 = Resistor [tolerance=±5% resistance=220 package="1206 [SMD]"]
  LED1 = smd LED [color="Red (633nm)" package="0805 [SMD]"]
  R4 = 12mm Trimmer Potentiometer (Large) [maximum_resistance=10kΩ knob_status=50% power=0.5W package=THT]
  R5 = 12mm Trimmer Potentiometer (Large) [maximum_resistance=10kΩ knob_status=50% power=0.5W package=THT]
  C1 = Electrolytic Capacitor [capacitance=0.1µF voltage=35V package="1010 [SMD, electrolytic]"]
  C2 = Electrolytic Capacitor [capacitance=0.1µF voltage=35V package="1010 [SMD, electrolytic]"]
  MUX1 = 74HC4051 [package="DIP (Dual Inline) [THT]"]
  MUX2 = 74HC4051 [package="DIP (Dual Inline) [THT]"]
  MUX3 = 74HC4051 [package="DIP (Dual Inline) [THT]"]

nets:
  N1: Part1.TXO, TRS1.Tip
  VSS: Part1.GND, OLED1.GND, TRS1.Sleeve, LED1.cathode, R4.wiper, R4.leg2, R5.wiper, R5.leg2, C1.-, C2.-, MUX1.VEE, MUX1.VSS, MUX2.VEE, MUX2.VSS, MUX3.VEE, MUX3.VSS
  N2: Part1.D2, OLED1.SDA
  N3: Part1.D3, OLED1.SCK
  N4: Part1.D4, MUX1.A, MUX2.A, MUX3.A
  N5: Part1.D6, LED1.anode
  N6: Part1.D7, MUX1.IO, MUX2.IO, MUX3.IO
  N7: Part1.D8, MUX1.C, MUX2.C, MUX3.C
  N8: Part1.D10, MUX3.INH
  N9: Part1.D16, MUX1.INH
  N10: Part1.D14, MUX2.INH
  N11: Part1.D15, MUX1.B, MUX2.B, MUX3.B
  N12: Part1.A1, R4.leg1, C1.+
  N13: Part1.A2, R5.leg1, C2.+
  VDD: Part1.VCC, OLED1.VDD, R3.Pin_1, MUX1.VDD, MUX2.VDD, MUX3.VDD
  N14: TRS1.Ring, R3.Pin_0

notes:
  MIDI OUTPUT
  (3.5mm TRS)
  MENU LED
  10k potentiometers factory wired as voltage dividers (wiper tied to one leg)
  Added 0.1uf capacitors to smooth voltage spikes
  MULTIPLEXER MAYHEM! 🌪️
  All buttons indexed 0-23
  (To save space, button grounds are not shown)
  2: Low Yellow
  1: Low Red
  0: Low Green
  3: Low Blue
  10: Neck Down
  9: High Orange
  8: High Blue
  11: Neck Up
  18: Start
  17: Left Arrow
  16: Down Arrow
  19: Select
  4: Low Orange
  6: High Red
  7: High Yellow
  5: High Green
  12: Bridge Down
  14: Up arrow
  15: Right Arrow
  13: Bridge Up
  20: Menu / Save
  22: Unused
  23: Unused
  21: Unused
  I2C OLED SSD Display
  Button indexes at a glance
  Fret Board....................0 - 9
  Strum Switches..........10 - 13
  Directional Keypad....14 - 17
  Menu Diving...............18 - 20
  Unused.......................21 - 23

custom parts:
  OLED 128x64 I2C Monochrome Display GND-VDD: OLED 128x64 I2C Monochrome Display. Note: there are two variants of this part, this one is the GND VDD SCK SDA variant. The other is VDD GND SCK SDA. Make sure you select the part that matches your module as using the incorrect part will probably destroy your module! In addition the mounting holes are marked on silkscreen but not by default drilled. If you want drilled mounting holes, copy a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
  74HC4051: 8 channel analog multiplexer/demultiplexer
